# Fritzing sketch Caja Negra v1 (saved by Fritzing 0.9.3b)
breadboards: 3

parts:
  SD_card_module1 = SD Card Module
  PCB2 = RTC_DS1302_module
  Componente1 = Arduino Nano (Rev3.0)
  R1 = Resistor [tolerance=±5% resistance=330 package=THT]
  R2 = Resistor [tolerance=±5% resistance=330 package=THT]
  R3 = Resistor [tolerance=±5% resistance=330 package=THT]
  R4 = Resistor [tolerance=±5% resistance=330 package=THT]
  Part1 = KY-009 Full Color RGB LED SMD Module [package="Breakout board"]
  S1 = Pushbutton [package="[SMD]"]

nets:
  GND: SD_card_module1.GND, PCB2.GND, Part1.-, S1.Pin_1, S1.Pin_2
  N1: SD_card_module1.+5, PCB2.VCC
  N2: SD_card_module1.CS, R1.Pin_1
  N3: SD_card_module1.MOSI, R4.Pin_1
  N4: SD_card_module1.SCK, R2.Pin_1
  N5: SD_card_module1.MISO, R3.Pin_1
  N6: PCB2.RST, Componente1.D2
  N7: PCB2.DAT, Componente1.D3
  N8: PCB2.CLK, Componente1.D5
  N9: Componente1.RESET, S1.Pin_3, S1.Pin_4
  N10: Componente1.D4, R1.Pin_0
  N11: Componente1.D7, Part1.R
  N12: Componente1.D8, Part1.G
  N13: Componente1.D9, Part1.B
  N14: Componente1.D11/MOSI, R4.Pin_0
  N15: Componente1.D12/MISO, R3.Pin_0
  N16: Componente1.D13/SCK, R2.Pin_0

notes:
  DATOS (Cable verde a RX)
  - Escucha serial de datos
  Configuración de RTC
  (Cables a A2 y A3)
  - La inicialización del módulo
  RTC se realiza por estos cables mediante conexión serial.
  Resistores:
  330 ohms

custom parts:
  SD Card Module: SD Card Module Slot Socket Reader For Arduino ARM MCU
  RTC_DS1302_module: Arduino module DS1302 SPI Real Time Clock
  KY-009 Full Color RGB LED SMD Module: RGB full color LED Module KY-009 for Arduino, emits a range of colors by mixing red, green and blue. The amount of each primary color is adjusted using PWM.
